# Fritzing sketch pumpreadout (saved by Fritzing 0.9.3b)
breadboards: 1

parts:
  Part1 = Intel Galileo Gen2
  U1 = LCD-16X2 [package=lcd-16x2]
  R1 = Resistor [tolerance=±5% resistance=220 package="2010 [SMD]"]

nets:
  N1: Part1.D11_PWM/MOSI, U1.E
  N2: Part1.D12/MISO, U1.RS
  GND: Part1.GND, U1.VSS, U1.VO, U1.K
  N3: Part1.D2, U1.DB7
  N4: Part1.D3_PWM, U1.DB6
  N5: Part1.D4, U1.DB5
  N6: Part1.D5_PWM, U1.DB4
  5V: Part1.5V, U1.VDD, R1.Pin_0
  N7: U1.A, R1.Pin_1
